# Fritzing sketch Christmas_Wraith (saved by Fritzing 0.9.3b)
breadboards: 1

parts:
  R1 = Resistor [tolerance=±5% resistance=100 package=THT]
  Bauteil1 = Arduino Uno (Rev3)
  R2 = Resistor [tolerance=±5% resistance=100 package=THT]
  R3 = Resistor [tolerance=±5% resistance=100 package=THT]
  R4 = Resistor [tolerance=±5% resistance=100 package=THT]
  LED1 = RGB LED (com. cathode, rgb) [package="5 mm [THT]"]
  LED2 = RGB LED (com. cathode, rgb) [package="5 mm [THT]"]
  LED3 = RGB LED (com. cathode, rgb) [package="5 mm [THT]"]
  LED4 = RGB LED (com. cathode, rgb) [package="5 mm [THT]"]

nets:
  N1: R1.Pin_0, Bauteil1.A1, Bauteil1.GND, R2.Pin_0, R3.Pin_0, R4.Pin_0
  N2: R1.Pin_1, LED3.green_anode
  N3: Bauteil1.D8, LED1.red_anode
  N4: Bauteil1.D9_PWM, LED1.common_cathode
  N5: Bauteil1.D10_PWM/SS, LED1.blue_anode
  N6: Bauteil1.D11_PWM/MOSI, LED4.red_anode
  N7: Bauteil1.D12/MISO, LED4.common_cathode
  N8: Bauteil1.D13/SCK, LED4.blue_anode
  N9: Bauteil1.D2, LED2.red_anode
  N10: Bauteil1.D3_PWM, LED2.common_cathode
  N11: Bauteil1.D4, LED2.blue_anode
  N12: Bauteil1.D5_PWM, LED3.red_anode
  N13: Bauteil1.D6_PWM, LED3.common_cathode
  N14: Bauteil1.D7, LED3.blue_anode
  N15: R2.Pin_1, LED1.green_anode
  N16: R3.Pin_1, LED4.green_anode
  N17: R4.Pin_1, LED2.green_anode
